// Logisim project active-high-rs-latches.circ as structural Verilog: 1 circuit, main circuit main
module main (
  input  R,
  input  S,
  input  R_2,
  input  S_2,
  output Q,
  output nQ,
  output Q_2,
  output nQ_2
);

  nor nor_1 (Q, R, nQ);
  nor nor_2 (nQ, Q, S);
  nand nand_1 (Q_2, R_2, nQ_2);
  nand nand_2 (nQ_2, Q_2, S_2);
endmodule
