// Logisim project cas_array_div.circ as structural Verilog: 5 circuits, main circuit CAS 
module ArrayDiv (
  input  A_9,
  input  B_4,
  input  A_8,
  input  B_3,
  input  A_7,
  input  B_2,
  input  A_6,
  input  B_1,
  input  A_5,
  input  B_0,
  input  A_4,
  input  A_3,
  input  A_3_2,
  input  A_2,
  input  A_1,
  input  A_0,
  output Q_4,
  output Q_3,
  output Q_2,
  output Q_1,
  output Q_0,
  output R_4,
  output R_3,
  output R_2,
  output R_1,
  output R_0
);

  wire cas_1_bout, cas_1_tout, cas_2_bout, cas_2_tout, cas_3_bout, cas_3_cout, cas_3_rout, cas_3_tout,
       cas_4_bout, cas_4_cout, cas_4_rout, cas_4_tout, cas_5_bout, cas_5_tout, cas_6_bout, cas_6_cout,
       cas_6_rout, cas_6_tout, cas_7_bout, cas_7_cout, cas_7_rout, cas_7_tout, cas_8_bout, cas_8_tout,
       cas_9_bout, cas_9_cout, cas_9_rout, cas_9_tout, cas_10_bout, cas_10_cout, cas_10_rout, cas_10_tout,
       cas_11_bout, cas_11_cout, cas_11_rout, cas_11_tout, cas_12_bout, cas_12_tout, cas_13_bout,
       cas_13_cout, cas_13_rout, cas_13_tout, cas_14_bout, cas_14_cout, cas_14_rout, cas_14_tout,
       cas_15_bout, cas_15_cout, cas_15_rout, cas_15_tout, cas_16_bout, cas_16_cout, cas_16_rout,
       cas_16_tout, cas_17_tout, cas_18_bout, cas_18_cout, cas_18_rout, cas_18_tout, cas_19_bout,
       cas_19_cout, cas_19_rout, cas_19_tout, cas_20_bout, cas_20_cout, cas_20_rout, cas_20_tout,
       cas_21_cout, cas_21_tout, cas_22_bout, cas_22_cout, cas_22_rout, cas_22_tout, cas_23_bout,
       cas_23_cout, cas_23_rout, cas_23_tout, cas_24_bout, cas_24_cout, cas_24_rout, cas_24_tout,
       cas_25_bout, cas_25_cout, cas_25_rout, cas_25_tout, cas_26_cout, cas_26_tout, cas_27_bout,
       cas_27_cout, cas_27_rout, cas_27_tout, cas_28_cout, cas_28_tout, cas_29_bout, cas_29_cout,
       cas_29_rout, cas_29_tout, cas_30_cout, cas_30_tout, undriven;

  // XOR_Gate xor_1 has open pins: in0=undriven, in1=A_9, out=open
  CAS cas_1 (.Bin(B_4), .Rin(A_8), .Cin(cas_3_cout), .Tout(cas_1_tout), .Bout(cas_1_bout));  // open: T, Cout, Rout
  CAS cas_2 (
    .Bin(cas_1_bout), .Rin(cas_3_rout), .Cin(cas_4_cout), .Tout(cas_2_tout), .Bout(cas_2_bout));  // open: T, Cout, Rout
  CAS cas_3 (
    .T(cas_1_tout), .Bin(B_3), .Rin(A_7), .Cin(cas_6_cout), .Cout(cas_3_cout), .Tout(cas_3_tout),
    .Rout(cas_3_rout), .Bout(cas_3_bout));
  CAS cas_4 (
    .T(cas_2_tout), .Bin(cas_3_bout), .Rin(cas_6_rout), .Cin(cas_10_cout), .Cout(cas_4_cout),
    .Tout(cas_4_tout), .Rout(cas_4_rout), .Bout(cas_4_bout));
  CAS cas_5 (
    .Bin(cas_2_bout), .Rin(cas_4_rout), .Cin(cas_7_cout), .Tout(cas_5_tout), .Bout(cas_5_bout));  // open: T, Cout, Rout
  CAS cas_6 (
    .T(cas_3_tout), .Bin(B_2), .Rin(A_6), .Cin(cas_9_cout), .Cout(cas_6_cout), .Tout(cas_6_tout),
    .Rout(cas_6_rout), .Bout(cas_6_bout));
  CAS cas_7 (
    .T(cas_5_tout), .Bin(cas_4_bout), .Rin(cas_10_rout), .Cin(cas_14_cout), .Cout(cas_7_cout),
    .Tout(cas_7_tout), .Rout(cas_7_rout), .Bout(cas_7_bout));
  CAS cas_8 (
    .Bin(cas_5_bout), .Rin(cas_7_rout), .Cin(cas_11_cout), .Tout(cas_8_tout), .Bout(cas_8_bout));  // open: T, Cout, Rout
  CAS cas_9 (
    .T(cas_6_tout), .Bin(B_1), .Rin(A_5), .Cin(cas_15_cout), .Cout(cas_9_cout), .Tout(cas_9_tout),
    .Rout(cas_9_rout), .Bout(cas_9_bout));
  CAS cas_10 (
    .T(cas_4_tout), .Bin(cas_6_bout), .Rin(cas_9_rout), .Cin(cas_13_cout), .Cout(cas_10_cout),
    .Tout(cas_10_tout), .Rout(cas_10_rout), .Bout(cas_10_bout));
  CAS cas_11 (
    .T(cas_8_tout), .Bin(cas_7_bout), .Rin(cas_14_rout), .Cin(cas_19_cout), .Cout(cas_11_cout),
    .Tout(cas_11_tout), .Rout(cas_11_rout), .Bout(cas_11_bout));
  CAS cas_12 (
    .Bin(cas_8_bout), .Rin(cas_11_rout), .Cin(cas_16_cout), .Tout(cas_12_tout), .Bout(cas_12_bout));  // open: T, Cout, Rout
  CAS cas_13 (
    .T(cas_10_tout), .Bin(cas_9_bout), .Rin(cas_15_rout), .Cin(cas_20_cout), .Cout(cas_13_cout),
    .Tout(cas_13_tout), .Rout(cas_13_rout), .Bout(cas_13_bout));
  CAS cas_14 (
    .T(cas_7_tout), .Bin(cas_10_bout), .Rin(cas_13_rout), .Cin(cas_18_cout), .Cout(cas_14_cout),
    .Tout(cas_14_tout), .Rout(cas_14_rout), .Bout(cas_14_bout));
  CAS cas_15 (
    .T(cas_9_tout), .Bin(B_0), .Rin(A_4), .Cin(cas_15_tout), .Cout(cas_15_cout), .Tout(cas_15_tout),
    .Rout(cas_15_rout), .Bout(cas_15_bout));
  CAS cas_16 (
    .T(cas_12_tout), .Bin(cas_11_bout), .Rin(cas_19_rout), .Cin(cas_23_cout), .Cout(cas_16_cout),
    .Tout(cas_16_tout), .Rout(cas_16_rout), .Bout(cas_16_bout));
  CAS cas_17 (
    .Bin(cas_12_bout), .Rin(cas_16_rout), .Cin(cas_21_cout), .Tout(cas_17_tout), .Rout(R_4));  // open: T, Cout, Bout
  CAS cas_18 (
    .T(cas_14_tout), .Bin(cas_13_bout), .Rin(cas_20_rout), .Cin(cas_24_cout), .Cout(cas_18_cout),
    .Tout(cas_18_tout), .Rout(cas_18_rout), .Bout(cas_18_bout));
  CAS cas_19 (
    .T(cas_11_tout), .Bin(cas_14_bout), .Rin(cas_18_rout), .Cin(cas_22_cout), .Cout(cas_19_cout),
    .Tout(cas_19_tout), .Rout(cas_19_rout), .Bout(cas_19_bout));
  CAS cas_20 (
    .T(cas_13_tout), .Bin(cas_15_bout), .Rin(A_3), .Cin(cas_20_tout), .Cout(cas_20_cout), .Tout(cas_20_tout),
    .Rout(cas_20_rout), .Bout(cas_20_bout));
  CAS cas_21 (
    .T(cas_17_tout), .Bin(cas_16_bout), .Rin(cas_23_rout), .Cin(cas_26_cout), .Cout(cas_21_cout),
    .Tout(cas_21_tout), .Rout(R_3));  // open: Bout
  CAS cas_22 (
    .T(cas_19_tout), .Bin(cas_18_bout), .Rin(cas_24_rout), .Cin(cas_27_cout), .Cout(cas_22_cout),
    .Tout(cas_22_tout), .Rout(cas_22_rout), .Bout(cas_22_bout));
  CAS cas_23 (
    .T(cas_16_tout), .Bin(cas_19_bout), .Rin(cas_22_rout), .Cin(cas_25_cout), .Cout(cas_23_cout),
    .Tout(cas_23_tout), .Rout(cas_23_rout), .Bout(cas_23_bout));
  CAS cas_24 (
    .T(cas_18_tout), .Bin(cas_20_bout), .Rin(A_3_2), .Cin(cas_24_tout), .Cout(cas_24_cout),
    .Tout(cas_24_tout), .Rout(cas_24_rout), .Bout(cas_24_bout));
  CAS cas_25 (
    .T(cas_23_tout), .Bin(cas_22_bout), .Rin(cas_27_rout), .Cin(cas_29_cout), .Cout(cas_25_cout),
    .Tout(cas_25_tout), .Rout(cas_25_rout), .Bout(cas_25_bout));
  CAS cas_26 (
    .T(cas_21_tout), .Bin(cas_23_bout), .Rin(cas_25_rout), .Cin(cas_28_cout), .Cout(cas_26_cout),
    .Tout(cas_26_tout), .Rout(R_2));  // open: Bout
  CAS cas_27 (
    .T(cas_22_tout), .Bin(cas_24_bout), .Rin(A_2), .Cin(cas_27_tout), .Cout(cas_27_cout), .Tout(cas_27_tout),
    .Rout(cas_27_rout), .Bout(cas_27_bout));
  CAS cas_28 (
    .T(cas_26_tout), .Bin(cas_25_bout), .Rin(cas_29_rout), .Cin(cas_30_cout), .Cout(cas_28_cout),
    .Tout(cas_28_tout), .Rout(R_1));  // open: Bout
  CAS cas_29 (
    .T(cas_25_tout), .Bin(cas_27_bout), .Rin(A_1), .Cin(cas_29_tout), .Cout(cas_29_cout), .Tout(cas_29_tout),
    .Rout(cas_29_rout), .Bout(cas_29_bout));
  CAS cas_30 (
    .T(cas_28_tout), .Bin(cas_29_bout), .Rin(A_0), .Cin(cas_30_tout), .Cout(cas_30_cout), .Tout(cas_30_tout),
    .Rout(R_0));  // open: Bout
endmodule

module CAS (
  input  Bin,
  input  Rin,
  input  T,
  input  Cin,
  output Tout,
  output Cout,
  output Bout,
  output Rout
);

  wire xor_1_out;

  xor xor_1 (xor_1_out, T, Bin);
  Adder #(.width(1)) adder_1 (.a(xor_1_out), .b(Rin), .out(Rout), .cin(Cin), .cout(Cout));

  assign Bout = Bin;
  assign Tout = T;

  // Notes on the sheet:
  //   T
  //   Cout
  //   Rout
  //   Rin
  //   Bout
  //   Cin
endmodule

module test (
  input  Bin,
  input  Rin,
  input  T,
  input  Cin,
  output Tout,
  output Cout,
  output Bout,
  output Rout
);

  wire xor_1_out;

  xor xor_1 (xor_1_out, T, Bin);
  Adder #(.width(1)) adder_1 (.a(xor_1_out), .b(Rin), .out(Rout), .cin(Cin), .cout(Cout));

  assign Bout = Bin;
  assign Tout = T;

  // Notes on the sheet:
  //   T
  //   Cout
  //   Rout
  //   Rin
  //   Bout
  //   Cin
endmodule

module testtt (
  input  B_5,
  input  A_10,
  input  B_4,
  input  A_9,
  input  B_3,
  input  A_8,
  input  B_2,
  input  A_7,
  input  B_1,
  input  A_6,
  input  B_0,
  input  A_5,
  input  A_11,
  input  A_4,
  input  A_3,
  input  A_2,
  input  A_1,
  input  A_0,
  output Q_5,
  output Q_4,
  output Q_3,
  output Q_2,
  output Q_1,
  output Q_0,
  output R_5,
  output R_4,
  output R_3,
  output R_2,
  output R_1,
  output R_0
);

  wire test_1_bout, test_1_tout, test_2_bout, test_2_cout, test_2_rout, test_2_tout, test_3_bout,
       test_3_tout, test_4_bout, test_4_cout, test_4_rout, test_4_tout, test_5_bout, test_5_cout,
       test_5_rout, test_5_tout, test_6_bout, test_6_tout, test_7_bout, test_7_cout, test_7_rout,
       test_7_tout, test_8_bout, test_8_cout, test_8_rout, test_8_tout, test_9_bout, test_9_cout,
       test_9_rout, test_9_tout, test_10_bout, test_10_tout, test_11_bout, test_11_cout, test_11_rout,
       test_11_tout, test_12_bout, test_12_cout, test_12_rout, test_12_tout, test_13_bout, test_13_cout,
       test_13_rout, test_13_tout, test_14_bout, test_14_cout, test_14_rout, test_14_tout, test_15_bout,
       test_15_tout, test_16_bout, test_16_cout, test_16_rout, test_16_tout, test_17_bout, test_17_cout,
       test_17_rout, test_17_tout, test_18_bout, test_18_cout, test_18_rout, test_18_tout, test_19_bout,
       test_19_cout, test_19_rout, test_19_tout, test_20_bout, test_20_cout, test_20_rout, test_20_tout,
       test_21_tout, test_22_bout, test_22_cout, test_22_rout, test_22_tout, test_23_bout, test_23_cout,
       test_23_rout, test_23_tout, test_24_bout, test_24_cout, test_24_rout, test_24_tout, test_25_bout,
       test_25_cout, test_25_rout, test_25_tout, test_26_cout, test_26_tout, test_27_bout, test_27_cout,
       test_27_rout, test_27_tout, test_28_bout, test_28_cout, test_28_rout, test_28_tout, test_29_bout,
       test_29_cout, test_29_rout, test_29_tout, test_30_cout, test_30_tout, test_31_bout, test_31_cout,
       test_31_rout, test_31_tout, test_32_bout, test_32_cout, test_32_rout, test_32_tout, test_33_cout,
       test_33_tout, test_34_bout, test_34_cout, test_34_rout, test_34_tout, test_35_cout, test_35_tout,
       test_36_cout, test_36_tout, xor_1_out;

  xor xor_1 (xor_1_out, B_5, ~A_11);  // XOR_Gate
  test test_1 (
    .T(xor_1_out), .Rin(A_10), .Tout(test_1_tout), .Cin(test_2_cout), .Cout(Q_5), .Bout(test_1_bout),
    .Bin(B_5));  // open: Rout
  test test_2 (
    .T(test_1_tout), .Rin(A_9), .Tout(test_2_tout), .Cin(test_4_cout), .Cout(test_2_cout),
    .Bout(test_2_bout), .Rout(test_2_rout), .Bin(B_4));
  test test_3 (
    .T(Q_5), .Rin(test_2_rout), .Tout(test_3_tout), .Cin(test_5_cout), .Cout(Q_4), .Bout(test_3_bout),
    .Bin(test_1_bout));  // open: Rout
  test test_4 (
    .T(test_2_tout), .Rin(A_8), .Tout(test_4_tout), .Cin(test_7_cout), .Cout(test_4_cout),
    .Bout(test_4_bout), .Rout(test_4_rout), .Bin(B_3));
  test test_5 (
    .T(test_3_tout), .Rin(test_4_rout), .Tout(test_5_tout), .Cin(test_8_cout), .Cout(test_5_cout),
    .Bout(test_5_bout), .Rout(test_5_rout), .Bin(test_2_bout));
  test test_6 (
    .T(Q_4), .Rin(test_5_rout), .Tout(test_6_tout), .Cin(test_9_cout), .Cout(Q_3), .Bout(test_6_bout),
    .Bin(test_3_bout));  // open: Rout
  test test_7 (
    .T(test_4_tout), .Rin(A_7), .Tout(test_7_tout), .Cin(test_11_cout), .Cout(test_7_cout),
    .Bout(test_7_bout), .Rout(test_7_rout), .Bin(B_2));
  test test_8 (
    .T(test_5_tout), .Rin(test_7_rout), .Tout(test_8_tout), .Cin(test_12_cout), .Cout(test_8_cout),
    .Bout(test_8_bout), .Rout(test_8_rout), .Bin(test_4_bout));
  test test_9 (
    .T(test_6_tout), .Rin(test_8_rout), .Tout(test_9_tout), .Cin(test_13_cout), .Cout(test_9_cout),
    .Bout(test_9_bout), .Rout(test_9_rout), .Bin(test_5_bout));
  test test_10 (
    .T(Q_3), .Rin(test_9_rout), .Tout(test_10_tout), .Cin(test_14_cout), .Cout(Q_2), .Bout(test_10_bout),
    .Bin(test_6_bout));  // open: Rout
  test test_11 (
    .T(test_7_tout), .Rin(A_6), .Tout(test_11_tout), .Cin(test_16_cout), .Cout(test_11_cout),
    .Bout(test_11_bout), .Rout(test_11_rout), .Bin(B_1));
  test test_12 (
    .T(test_8_tout), .Rin(test_11_rout), .Tout(test_12_tout), .Cin(test_17_cout), .Cout(test_12_cout),
    .Bout(test_12_bout), .Rout(test_12_rout), .Bin(test_7_bout));
  test test_13 (
    .T(test_9_tout), .Rin(test_12_rout), .Tout(test_13_tout), .Cin(test_18_cout), .Cout(test_13_cout),
    .Bout(test_13_bout), .Rout(test_13_rout), .Bin(test_8_bout));
  test test_14 (
    .T(test_10_tout), .Rin(test_13_rout), .Tout(test_14_tout), .Cin(test_19_cout), .Cout(test_14_cout),
    .Bout(test_14_bout), .Rout(test_14_rout), .Bin(test_9_bout));
  test test_15 (
    .T(Q_2), .Rin(test_14_rout), .Tout(test_15_tout), .Cin(test_20_cout), .Cout(Q_1), .Bout(test_15_bout),
    .Bin(test_10_bout));  // open: Rout
  test test_16 (
    .T(test_11_tout), .Rin(A_5), .Tout(test_16_tout), .Cin(test_16_tout), .Cout(test_16_cout),
    .Bout(test_16_bout), .Rout(test_16_rout), .Bin(B_0));
  test test_17 (
    .T(test_12_tout), .Rin(test_16_rout), .Tout(test_17_tout), .Cin(test_22_cout), .Cout(test_17_cout),
    .Bout(test_17_bout), .Rout(test_17_rout), .Bin(test_11_bout));
  test test_18 (
    .T(test_13_tout), .Rin(test_17_rout), .Tout(test_18_tout), .Cin(test_23_cout), .Cout(test_18_cout),
    .Bout(test_18_bout), .Rout(test_18_rout), .Bin(test_12_bout));
  test test_19 (
    .T(test_14_tout), .Rin(test_18_rout), .Tout(test_19_tout), .Cin(test_24_cout), .Cout(test_19_cout),
    .Bout(test_19_bout), .Rout(test_19_rout), .Bin(test_13_bout));
  test test_20 (
    .T(test_15_tout), .Rin(test_19_rout), .Tout(test_20_tout), .Cin(test_25_cout), .Cout(test_20_cout),
    .Bout(test_20_bout), .Rout(test_20_rout), .Bin(test_14_bout));
  test test_21 (
    .T(Q_1), .Rin(test_20_rout), .Tout(test_21_tout), .Cin(test_26_cout), .Cout(Q_0), .Rout(R_5),
    .Bin(test_15_bout));  // open: Bout
  test test_22 (
    .T(test_17_tout), .Rin(A_4), .Tout(test_22_tout), .Cin(test_22_tout), .Cout(test_22_cout),
    .Bout(test_22_bout), .Rout(test_22_rout), .Bin(test_16_bout));
  test test_23 (
    .T(test_18_tout), .Rin(test_22_rout), .Tout(test_23_tout), .Cin(test_27_cout), .Cout(test_23_cout),
    .Bout(test_23_bout), .Rout(test_23_rout), .Bin(test_17_bout));
  test test_24 (
    .T(test_19_tout), .Rin(test_23_rout), .Tout(test_24_tout), .Cin(test_28_cout), .Cout(test_24_cout),
    .Bout(test_24_bout), .Rout(test_24_rout), .Bin(test_18_bout));
  test test_25 (
    .T(test_20_tout), .Rin(test_24_rout), .Tout(test_25_tout), .Cin(test_29_cout), .Cout(test_25_cout),
    .Bout(test_25_bout), .Rout(test_25_rout), .Bin(test_19_bout));
  test test_26 (
    .T(test_21_tout), .Rin(test_25_rout), .Tout(test_26_tout), .Cin(test_30_cout), .Cout(test_26_cout),
    .Rout(R_4), .Bin(test_20_bout));  // open: Bout
  test test_27 (
    .T(test_23_tout), .Rin(A_3), .Tout(test_27_tout), .Cin(test_27_tout), .Cout(test_27_cout),
    .Bout(test_27_bout), .Rout(test_27_rout), .Bin(test_22_bout));
  test test_28 (
    .T(test_24_tout), .Rin(test_27_rout), .Tout(test_28_tout), .Cin(test_31_cout), .Cout(test_28_cout),
    .Bout(test_28_bout), .Rout(test_28_rout), .Bin(test_23_bout));
  test test_29 (
    .T(test_25_tout), .Rin(test_28_rout), .Tout(test_29_tout), .Cin(test_32_cout), .Cout(test_29_cout),
    .Bout(test_29_bout), .Rout(test_29_rout), .Bin(test_24_bout));
  test test_30 (
    .T(test_26_tout), .Rin(test_29_rout), .Tout(test_30_tout), .Cin(test_33_cout), .Cout(test_30_cout),
    .Rout(R_3), .Bin(test_25_bout));  // open: Bout
  test test_31 (
    .T(test_28_tout), .Rin(A_2), .Tout(test_31_tout), .Cin(test_31_tout), .Cout(test_31_cout),
    .Bout(test_31_bout), .Rout(test_31_rout), .Bin(test_27_bout));
  test test_32 (
    .T(test_29_tout), .Rin(test_31_rout), .Tout(test_32_tout), .Cin(test_34_cout), .Cout(test_32_cout),
    .Bout(test_32_bout), .Rout(test_32_rout), .Bin(test_28_bout));
  test test_33 (
    .T(test_30_tout), .Rin(test_32_rout), .Tout(test_33_tout), .Cin(test_35_cout), .Cout(test_33_cout),
    .Rout(R_2), .Bin(test_29_bout));  // open: Bout
  test test_34 (
    .T(test_32_tout), .Rin(A_1), .Tout(test_34_tout), .Cin(test_34_tout), .Cout(test_34_cout),
    .Bout(test_34_bout), .Rout(test_34_rout), .Bin(test_31_bout));
  test test_35 (
    .T(test_33_tout), .Rin(test_34_rout), .Tout(test_35_tout), .Cin(test_36_cout), .Cout(test_35_cout),
    .Rout(R_1), .Bin(test_32_bout));  // open: Bout
  test test_36 (
    .T(test_35_tout), .Rin(A_0), .Tout(test_36_tout), .Cin(test_36_tout), .Cout(test_36_cout), .Rout(R_0),
    .Bin(test_34_bout));  // open: Bout
endmodule

module Arraytest_klein (
  input  B5,
  input  B4,
  input  B3,
  input  B2,
  input  B1,
  input  A11,
  input  A10,
  input  A9,
  input  A8,
  input  A7,
  input  A6,
  input  A5,
  input  B0,
  input  A4,
  input  A3,
  input  A2,
  input  A1,
  input  A0,
  output Q5,
  output Q4,
  output Q3,
  output Q2,
  output Q1,
  output Q0,
  output R5,
  output R4,
  output R3,
  output R2,
  output R1,
  output Ro
);

  testtt testtt_1 (
    .Q_5(Q5), .Q_4(Q4), .Q_3(Q3), .Q_2(Q2), .Q_1(Q1), .Q_0(Q0), .A_11(A11), .B_5(B5), .A_10(A10), .B_4(B4),
    .A_9(A9), .B_3(B3), .A_8(A8), .B_2(B2), .A_7(A7), .B_1(B1), .A_6(A6), .B_0(B0), .A_5(A5), .A_4(A4),
    .A_3(A3), .A_2(A2), .A_1(A1), .A_0(A0), .R_5(R5), .R_4(R4), .R_3(R3), .R_2(R2), .R_1(R1), .R_0(Ro));
endmodule
