// Logisim project cas_array_div.circ as structural Verilog: 2 circuits, main circuit CAS 
module ArrayDiv (
  input  B_4,
  input  A_7,
  input  B_3,
  input  A_6,
  input  B_2,
  input  A_5,
  input  B_1,
  input  A_4,
  input  B_0,
  input  A_3,
  input  A_8,
  input  A_2,
  input  A_1,
  input  A_0,
  output Q_3,
  output Q_2,
  output Q_1,
  output Q_0,
  output R_4,
  output R_3,
  output R_2,
  output R_1,
  output R_0
);

  wire cas_1_bout, cas_1_tout, cas_2_bout, cas_2_cout, cas_2_rout, cas_2_tout, cas_3_bout, cas_3_tout,
       cas_4_bout, cas_4_tout, cas_5_bout, cas_5_cout, cas_5_rout, cas_5_tout, cas_6_bout, cas_6_cout,
       cas_6_rout, cas_6_tout, cas_7_bout, cas_7_cout, cas_7_rout, cas_7_tout, cas_8_tout, cas_9_bout,
       cas_9_cout, cas_9_rout, cas_9_tout, cas_10_bout, cas_10_cout, cas_10_rout, cas_10_tout, cas_11_cout,
       cas_11_tout, cas_12_bout, cas_12_cout, cas_12_rout, cas_12_tout, cas_13_bout, cas_13_cout,
       cas_13_rout, cas_13_tout, cas_14_bout, cas_14_cout, cas_14_rout, cas_14_tout, cas_15_bout,
       cas_15_cout, cas_15_rout, cas_15_tout, cas_16_bout, cas_16_cout, cas_16_rout, cas_16_tout,
       cas_17_cout, cas_17_tout, cas_18_cout, cas_18_tout, cas_19_bout, cas_19_cout, cas_19_rout,
       cas_19_tout, cas_20_cout, cas_20_tout, xor_1_out;

  xor xor_1 (xor_1_out, B_4, ~A_8);  // XOR_Gate
  CAS cas_1 (
    .T(xor_1_out), .Bin(B_4), .Rin(A_7), .Cin(cas_2_cout), .Cout(Q_3), .Tout(cas_1_tout), .Bout(cas_1_bout));  // open: Rout
  CAS cas_2 (
    .T(cas_1_tout), .Bin(B_3), .Rin(A_6), .Cin(cas_6_cout), .Cout(cas_2_cout), .Tout(cas_2_tout),
    .Rout(cas_2_rout), .Bout(cas_2_bout));
  CAS cas_3 (
    .T(Q_3), .Bin(cas_1_bout), .Rin(cas_2_rout), .Cin(cas_5_cout), .Cout(Q_2), .Tout(cas_3_tout),
    .Bout(cas_3_bout));  // open: Rout
  CAS cas_4 (
    .T(Q_2), .Bin(cas_3_bout), .Rin(cas_5_rout), .Cin(cas_7_cout), .Cout(Q_1), .Tout(cas_4_tout),
    .Bout(cas_4_bout));  // open: Rout
  CAS cas_5 (
    .T(cas_3_tout), .Bin(cas_2_bout), .Rin(cas_6_rout), .Cin(cas_10_cout), .Cout(cas_5_cout),
    .Tout(cas_5_tout), .Rout(cas_5_rout), .Bout(cas_5_bout));
  CAS cas_6 (
    .T(cas_2_tout), .Bin(B_2), .Rin(A_5), .Cin(cas_9_cout), .Cout(cas_6_cout), .Tout(cas_6_tout),
    .Rout(cas_6_rout), .Bout(cas_6_bout));
  CAS cas_7 (
    .T(cas_4_tout), .Bin(cas_5_bout), .Rin(cas_10_rout), .Cin(cas_14_cout), .Cout(cas_7_cout),
    .Tout(cas_7_tout), .Rout(cas_7_rout), .Bout(cas_7_bout));
  CAS cas_8 (
    .T(Q_1), .Bin(cas_4_bout), .Rin(cas_7_rout), .Cin(cas_11_cout), .Cout(Q_0), .Tout(cas_8_tout), .Rout(R_4));  // open: Bout
  CAS cas_9 (
    .T(cas_6_tout), .Bin(B_1), .Rin(A_4), .Cin(cas_12_cout), .Cout(cas_9_cout), .Tout(cas_9_tout),
    .Rout(cas_9_rout), .Bout(cas_9_bout));
  CAS cas_10 (
    .T(cas_5_tout), .Bin(cas_6_bout), .Rin(cas_9_rout), .Cin(cas_13_cout), .Cout(cas_10_cout),
    .Tout(cas_10_tout), .Rout(cas_10_rout), .Bout(cas_10_bout));
  CAS cas_11 (
    .T(cas_8_tout), .Bin(cas_7_bout), .Rin(cas_14_rout), .Cin(cas_17_cout), .Cout(cas_11_cout),
    .Tout(cas_11_tout), .Rout(R_3));  // open: Bout
  CAS cas_12 (
    .T(cas_9_tout), .Bin(B_0), .Rin(A_3), .Cin(cas_12_tout), .Cout(cas_12_cout), .Tout(cas_12_tout),
    .Rout(cas_12_rout), .Bout(cas_12_bout));
  CAS cas_13 (
    .T(cas_10_tout), .Bin(cas_9_bout), .Rin(cas_12_rout), .Cin(cas_15_cout), .Cout(cas_13_cout),
    .Tout(cas_13_tout), .Rout(cas_13_rout), .Bout(cas_13_bout));
  CAS cas_14 (
    .T(cas_7_tout), .Bin(cas_10_bout), .Rin(cas_13_rout), .Cin(cas_16_cout), .Cout(cas_14_cout),
    .Tout(cas_14_tout), .Rout(cas_14_rout), .Bout(cas_14_bout));
  CAS cas_15 (
    .T(cas_13_tout), .Bin(cas_12_bout), .Rin(A_2), .Cin(cas_15_tout), .Cout(cas_15_cout), .Tout(cas_15_tout),
    .Rout(cas_15_rout), .Bout(cas_15_bout));
  CAS cas_16 (
    .T(cas_14_tout), .Bin(cas_13_bout), .Rin(cas_15_rout), .Cin(cas_19_cout), .Cout(cas_16_cout),
    .Tout(cas_16_tout), .Rout(cas_16_rout), .Bout(cas_16_bout));
  CAS cas_17 (
    .T(cas_11_tout), .Bin(cas_14_bout), .Rin(cas_16_rout), .Cin(cas_18_cout), .Cout(cas_17_cout),
    .Tout(cas_17_tout), .Rout(R_2));  // open: Bout
  CAS cas_18 (
    .T(cas_17_tout), .Bin(cas_16_bout), .Rin(cas_19_rout), .Cin(cas_20_cout), .Cout(cas_18_cout),
    .Tout(cas_18_tout), .Rout(R_1));  // open: Bout
  CAS cas_19 (
    .T(cas_16_tout), .Bin(cas_15_bout), .Rin(A_1), .Cin(cas_19_tout), .Cout(cas_19_cout), .Tout(cas_19_tout),
    .Rout(cas_19_rout), .Bout(cas_19_bout));
  CAS cas_20 (
    .T(cas_18_tout), .Bin(cas_19_bout), .Rin(A_0), .Cin(cas_20_tout), .Cout(cas_20_cout), .Tout(cas_20_tout),
    .Rout(R_0));  // open: Bout
endmodule

module CAS (
  input  Bin,
  input  Rin,
  input  T,
  input  Cin,
  output Tout,
  output Cout,
  output Bout,
  output Rout
);

  wire xor_1_out;

  xor xor_1 (xor_1_out, T, Bin);
  Adder #(.width(1)) adder_1 (.a(xor_1_out), .b(Rin), .out(Rout), .cin(Cin), .cout(Cout));

  assign Bout = Bin;
  assign Tout = T;

  // Notes on the sheet:
  //   T
  //   Cout
  //   Rout
  //   Rin
  //   Bout
  //   Cin
endmodule
