// Logisim project cmos_transmission_gate.circ as structural Verilog: 1 circuit, main circuit main
module main (
  input  y,
  input  x,
  output out_3
);

  wire not_1_out, not_2_out;

  Transistor transistor_1 (.in(not_1_out), .out(out_3), .gate(y));
  not not_1 (not_1_out, x);
  Transistor #(.\type ("n"), .gate("br")) transistor_2 (.in(not_1_out), .out(out_3), .gate(not_2_out));
  not not_2 (not_2_out, y);
  Transistor transistor_3 (.in(x), .out(out_3), .gate(not_2_out));
  Transistor #(.\type ("n"), .gate("br")) transistor_4 (.in(x), .out(out_3), .gate(y));
endmodule
